// Logisim project NCR Calculator.circ as structural Verilog: 3 circuits, main circuit main
module main (
  input  [2:0] in_1,
  input  [2:0] in_2
);

  wire A_B_out, A_prime_C_prime_B_prime_out, A_prime_C_prime_EF_out, A_prime_C_prime_out,
       A_prime_D_prime_out, and_1_out, and_2_out, B_prime_C_prime_F_prime_out, B_prime_DE_prime_F_out,
       B_prime_DE_prime_out, C_prime_D_prime_E_out, CF_out, D_prime_E_out, DF_prime_out, display_1_a,
       display_1_b, display_1_c, display_1_d, display_1_e, display_1_f, display_1_g, display_2_a,
       display_2_b, display_2_c, display_2_d, display_2_e, display_2_f, display_2_g, E_B_out,
       E_prime_F_prime_out, EF_out, EF_prime_out, F_D_C_out, F_prime_E_B_out, not_1_out, not_2_out,
       not_3_out, not_4_out, not_5_out, not_6_out, not_7_out, not_8_out, not_9_out, not_10_out, or_1_out,
       or_2_out, or_3_out, or_4_out, or_5_out;
  wire [5:0] circuit_1_f6;

  _7_Segment_Display u_7_segment_display_1 (
    .g(display_1_g), .f(display_1_e), .a(display_1_f), .b(display_1_a), .e(display_1_d), .d(display_1_c),
    .c(display_1_b));  // open: dp
  display display_1 (
    .x(in_1[2]), .y(in_1[1]), .z(in_1[0]), .a(display_1_a), .b(display_1_b), .c(display_1_c),
    .d(display_1_d), .e(display_1_e), .f(display_1_f), .g(display_1_g));
  display display_2 (
    .x(in_2[2]), .y(in_2[1]), .z(in_2[0]), .a(display_2_a), .b(display_2_b), .c(display_2_c),
    .d(display_2_d), .e(display_2_e), .f(display_2_f), .g(display_2_g));
  _7_Segment_Display u_7_segment_display_2 (
    .g(display_2_g), .f(display_2_e), .a(display_2_f), .b(display_2_a), .e(display_2_d), .d(display_2_c),
    .c(display_2_b));  // open: dp
  circuit circuit_1 (
    .a(in_1[2]), .b(in_1[1]), .c(in_1[0]), .d(in_2[2]), .e(in_2[1]), .f(in_2[0]), .f1(circuit_1_f6[5]),
    .f2(circuit_1_f6[4]), .f3(circuit_1_f6[3]), .f4(circuit_1_f6[2]), .f5(circuit_1_f6[1]),
    .f6(circuit_1_f6[0]));
  not not_1 (not_1_out, circuit_1_f6[3]);
  and EF (EF_out, circuit_1_f6[1], circuit_1_f6[0]);
  and D_prime_E (D_prime_E_out, circuit_1_f6[1], not_2_out);
  not not_2 (not_2_out, circuit_1_f6[2]);
  not not_3 (not_3_out, circuit_1_f6[1]);
  and CF (CF_out, circuit_1_f6[0], circuit_1_f6[3]);
  not not_4 (not_4_out, circuit_1_f6[0]);
  and B_prime_C_prime_F_prime (B_prime_C_prime_F_prime_out, not_10_out, not_4_out, not_1_out);
  not not_5 (not_5_out, circuit_1_f6[2]);
  and A_prime_D_prime (A_prime_D_prime_out, not_8_out, not_2_out);
  or F_D_C (F_D_C_out, circuit_1_f6[0], circuit_1_f6[2], circuit_1_f6[3]);
  and B_prime_DE_prime (B_prime_DE_prime_out, not_10_out, circuit_1_f6[2], not_3_out);
  and DF_prime (DF_prime_out, not_4_out, circuit_1_f6[2]);
  and C_prime_D_prime_E (C_prime_D_prime_E_out, not_1_out, not_5_out, circuit_1_f6[1]);
  not not_6 (not_6_out, circuit_1_f6[0]);
  not not_7 (not_7_out, circuit_1_f6[1]);
  not not_8 (not_8_out, circuit_1_f6[5]);
  or A_B (A_B_out, circuit_1_f6[4], circuit_1_f6[5]);
  and and_1 (and_1_out, not_6_out, circuit_1_f6[4]);
  and E_prime_F_prime (E_prime_F_prime_out, not_6_out, not_7_out);
  not not_9 (not_9_out, circuit_1_f6[3]);
  not not_10 (not_10_out, circuit_1_f6[4]);
  and A_prime_C_prime (A_prime_C_prime_out, not_8_out, not_9_out);
  and A_prime_C_prime_B_prime (A_prime_C_prime_B_prime_out, A_prime_C_prime_out, not_10_out);
  and and_2 (and_2_out, not_10_out, circuit_1_f6[2], circuit_1_f6[0]);
  or or_1 (or_1_out, B_prime_DE_prime_out, CF_out, B_prime_C_prime_F_prime_out, C_prime_D_prime_E_out);
  and EF_prime (EF_prime_out, circuit_1_f6[1], not_6_out);
  and A_prime_C_prime_EF (A_prime_C_prime_EF_out, A_prime_C_prime_out, EF_out);
  or or_2 (or_2_out, and_2_out, circuit_1_f6[1], and_1_out);
  or or_3 (or_3_out, B_prime_DE_prime_F_out, D_prime_E_out, EF_prime_out, and_1_out, circuit_1_f6[3]);
  or or_4 (or_4_out, circuit_1_f6[4], A_prime_D_prime_out, E_prime_F_prime_out, A_prime_C_prime_EF_out);
  and F_prime_E_B (F_prime_E_B_out, not_6_out, E_B_out);
  or E_B (E_B_out, circuit_1_f6[1], circuit_1_f6[4]);
  and B_prime_DE_prime_F (B_prime_DE_prime_F_out, not_10_out, not_3_out, circuit_1_f6[0], circuit_1_f6[2]);
  _7_Segment_Display u_7_segment_display_3 (
    .g(A_B_out), .f(A_prime_C_prime_B_prime_out), .a(not_9_out), .b(1'b1), .e(A_prime_C_prime_out),
    .d(not_9_out), .c(not_10_out));  // open: dp
  or or_5 (or_5_out, DF_prime_out, B_prime_DE_prime_out, circuit_1_f6[3], circuit_1_f6[5]);
  _7_Segment_Display u_7_segment_display_4 (
    .g(or_1_out), .f(or_5_out), .a(or_2_out), .b(or_4_out), .e(F_prime_E_B_out), .d(or_3_out), .c(F_D_C_out));  // open: dp

  // Notes on the sheet:
  //   E'
  //   Binomial Co-efficient
  //   D
  //   ABCDEF
  //   F
  //   E
  //   C
  //   B
  //   A
  //   F'
  //   BF'
  //   C'
  //   B'
  //   B'DF
  //   E + BF' + B'DF
endmodule

module circuit (
  input  a,
  input  b,
  input  c,
  input  d,
  input  e,
  input  f,
  output f1,
  output f2,
  output f3,
  output f4,
  output f5,
  output f6
);

  wire and_1_out, and_2_out, and_3_out, and_4_out, and_5_out, and_6_out, and_7_out, and_8_out, and_9_out,
       and_10_out, and_11_out, and_12_out, and_13_out, and_14_out, and_15_out, and_16_out, and_17_out,
       and_18_out, and_19_out, and_20_out, and_21_out, and_22_out, and_23_out, and_24_out, and_25_out,
       and_26_out, and_27_out, and_28_out, and_29_out, not_1_out, not_2_out, not_3_out, not_4_out, not_5_out,
       not_6_out, not_7_out, not_8_out, not_9_out, not_10_out, not_11_out, not_12_out, not_13_out,
       not_14_out, not_15_out, not_16_out, not_17_out, not_18_out, not_19_out, not_20_out, not_21_out,
       not_22_out, not_23_out, not_24_out, not_25_out, not_26_out, not_27_out, not_28_out, not_29_out,
       not_30_out, not_31_out, not_32_out, not_33_out, not_34_out, not_35_out, not_36_out, not_37_out,
       not_38_out, not_39_out, not_40_out, not_41_out, not_42_out, not_43_out, not_44_out, not_45_out,
       not_46_out, not_47_out, not_48_out, not_49_out, not_50_out, not_51_out, not_52_out, not_53_out,
       not_54_out;

  not not_1 (not_1_out, d);
  not not_2 (not_2_out, e);
  not not_3 (not_3_out, f);
  not not_4 (not_4_out, d);
  not not_5 (not_5_out, e);
  not not_6 (not_6_out, c);
  not not_7 (not_7_out, d);
  not not_8 (not_8_out, b);
  not not_9 (not_9_out, e);
  not not_10 (not_10_out, f);
  not not_11 (not_11_out, e);
  not not_12 (not_12_out, c);
  not not_13 (not_13_out, e);
  not not_14 (not_14_out, f);
  not not_15 (not_15_out, b);
  not not_16 (not_16_out, c);
  not not_17 (not_17_out, e);
  not not_18 (not_18_out, f);
  not not_19 (not_19_out, d);
  not not_20 (not_20_out, e);
  not not_21 (not_21_out, d);
  not not_22 (not_22_out, f);
  not not_23 (not_23_out, d);
  not not_24 (not_24_out, e);
  not not_25 (not_25_out, f);
  not not_26 (not_26_out, e);
  not not_27 (not_27_out, f);
  and and_1 (and_1_out, a, b, c, not_1_out, e, f);
  and and_2 (and_2_out, a, b, c, d, not_2_out, not_3_out);
  not not_28 (not_28_out, c);
  not not_29 (not_29_out, d);
  not not_30 (not_30_out, d);
  not not_31 (not_31_out, f);
  not not_32 (not_32_out, e);
  not not_33 (not_33_out, b);
  not not_34 (not_34_out, d);
  not not_35 (not_35_out, c);
  not not_36 (not_36_out, d);
  not not_37 (not_37_out, f);
  not not_38 (not_38_out, c);
  not not_39 (not_39_out, e);
  not not_40 (not_40_out, f);
  and and_3 (and_3_out, a, not_4_out, not_5_out, f);
  and and_4 (and_4_out, a, not_6_out, not_7_out, e);
  and and_5 (and_5_out, a, not_8_out, c, d, not_9_out, not_10_out);
  and and_6 (and_6_out, a, b, not_11_out, f);
  and and_7 (and_7_out, a, b, not_12_out, d, not_13_out);
  and and_8 (and_8_out, a, b, c, e, not_14_out);
  not not_41 (not_41_out, d);
  not not_42 (not_42_out, e);
  not not_43 (not_43_out, a);
  not not_44 (not_44_out, d);
  not not_45 (not_45_out, f);
  not not_46 (not_46_out, c);
  not not_47 (not_47_out, d);
  not not_48 (not_48_out, f);
  not not_49 (not_49_out, b);
  not not_50 (not_50_out, d);
  not not_51 (not_51_out, c);
  not not_52 (not_52_out, e);
  not not_53 (not_53_out, d);
  not not_54 (not_54_out, f);
  and and_9 (and_9_out, not_15_out, not_16_out, d, not_17_out, not_18_out);
  and and_10 (and_10_out, c, not_19_out, not_20_out);
  and and_11 (and_11_out, b, not_21_out, not_22_out);
  and and_12 (and_12_out, b, c, not_23_out);
  and and_13 (and_13_out, a, not_24_out, not_25_out);
  and and_14 (and_14_out, a, c, not_26_out);
  and and_15 (and_15_out, a, b, not_27_out);
  and and_16 (and_16_out, a, b, c);
  or or_1 (f1, and_1_out, and_2_out);
  and and_17 (and_17_out, a, b, not_28_out, not_29_out, e, f);
  and and_18 (and_18_out, a, b, c, not_30_out, e, not_31_out);
  or or_2 (f2, and_17_out, and_18_out, and_19_out);
  and and_19 (and_19_out, a, b, c, d, not_32_out, f);
  and and_20 (and_20_out, a, not_33_out, c, not_34_out, e);
  and and_21 (and_21_out, a, b, not_35_out, not_36_out, e, not_37_out);
  and and_22 (and_22_out, a, b, not_38_out, d, not_39_out, not_40_out);
  or or_3 (f4, and_3_out, and_4_out, and_5_out, and_6_out, and_7_out, and_8_out);
  and and_23 (and_23_out, b, not_41_out, not_42_out, f);
  and and_24 (and_24_out, not_43_out, b, c, not_44_out, e, not_45_out);
  and and_25 (and_25_out, a, not_46_out, not_47_out, e, not_48_out);
  and and_26 (and_26_out, a, not_49_out, c, not_50_out, e);
  and and_27 (and_27_out, a, b, not_51_out, d, not_52_out);
  and and_28 (and_28_out, a, b, c, not_53_out, f);
  and and_29 (and_29_out, a, b, c, d, not_54_out);
  or or_4 (f6, and_9_out, and_10_out, and_11_out, and_12_out, and_13_out, and_14_out, and_15_out, and_16_out);
  or or_5 (f3, and_20_out, and_21_out, and_22_out);
  or or_6 (f5, and_23_out, and_24_out, and_25_out, and_26_out, and_27_out, and_28_out, and_29_out);

  // Notes on the sheet:
  //   Binomial circuit
endmodule

module display (
  input  x,
  input  y,
  input  z,
  output a,
  output b,
  output c,
  output d,
  output e,
  output f,
  output g
);

  wire and_1_out, and_2_out, and_3_out, and_4_out, and_5_out, and_6_out, and_7_out, and_8_out, and_9_out,
       and_10_out, and_11_out, and_12_out, and_13_out, and_14_out, and_15_out, and_16_out, not_1_out,
       not_2_out, not_3_out, not_4_out, not_5_out, not_6_out, not_7_out, not_8_out, not_9_out, not_10_out,
       not_11_out, not_12_out, not_13_out, not_14_out, not_15_out, not_16_out, not_17_out, not_18_out,
       not_19_out, not_20_out, not_21_out;

  not not_1 (not_1_out, y);
  not not_2 (not_2_out, z);
  not not_3 (not_3_out, y);
  not not_4 (not_4_out, x);
  not not_5 (not_5_out, z);
  not not_6 (not_6_out, x);
  not not_7 (not_7_out, z);
  not not_8 (not_8_out, y);
  not not_9 (not_9_out, x);
  not not_10 (not_10_out, z);
  not not_11 (not_11_out, z);
  not not_12 (not_12_out, y);
  not not_13 (not_13_out, z);
  not not_14 (not_14_out, y);
  not not_15 (not_15_out, z);
  not not_16 (not_16_out, x);
  not not_17 (not_17_out, z);
  not not_18 (not_18_out, x);
  not not_19 (not_19_out, y);
  not not_20 (not_20_out, z);
  not not_21 (not_21_out, x);
  and and_1 (and_1_out, not_1_out, not_2_out);
  and and_2 (and_2_out, y, z);
  or or_1 (b, not_3_out, z, x);
  and and_3 (and_3_out, not_4_out, not_5_out);
  and and_4 (and_4_out, not_6_out, y);
  and and_5 (and_5_out, y, not_7_out);
  and and_6 (and_6_out, x, not_8_out, z);
  and and_7 (and_7_out, not_9_out, not_10_out);
  and and_8 (and_8_out, y, not_11_out);
  and and_9 (and_9_out, not_12_out, not_13_out);
  and and_10 (and_10_out, x, not_14_out);
  and and_11 (and_11_out, x, not_15_out);
  and and_12 (and_12_out, not_16_out, not_17_out);
  and and_13 (and_13_out, x, z);
  and and_14 (and_14_out, not_18_out, y);
  and and_15 (and_15_out, x, not_19_out);
  and and_16 (and_16_out, x, not_20_out);
  or or_2 (a, not_21_out, and_1_out, and_2_out);
  or or_3 (c, and_3_out, and_4_out, and_5_out, and_6_out);
  or or_4 (d, and_7_out, and_8_out);
  or or_5 (e, and_9_out, and_10_out, and_11_out);
  or or_6 (f, and_12_out, y, and_13_out);
  or or_7 (g, and_14_out, and_15_out, and_16_out);

  // Notes on the sheet:
  //   Display circuit
endmodule
