// Logisim project ncr2.circ as structural Verilog: 2 circuits, main circuit main
module main (
  input  [2:0] in_1,
  input  [2:0] in_2,
  output [5:0] out_3,
  output [5:0] out_4,
  output [5:0] out_5,
  output [5:0] out_6
);

  wire display_1_a, display_1_b, display_1_c, display_1_d, display_1_e, display_1_f, display_1_g,
       display_2_a, display_2_b, display_2_c, display_2_d, display_2_e, display_2_f, display_2_g;

  _7_Segment_Display u_7_segment_display_1 (
    .g(display_1_g), .f(display_1_e), .a(display_1_f), .b(display_1_a), .e(display_1_d), .d(display_1_c),
    .c(display_1_b));  // open: dp
  display display_1 (
    .x(in_1[2]), .y(in_1[1]), .z(in_1[0]), .a(display_1_a), .b(display_1_b), .c(display_1_c),
    .d(display_1_d), .e(display_1_e), .f(display_1_f), .g(display_1_g));
  display display_2 (
    .x(in_2[2]), .y(in_2[1]), .z(in_2[0]), .a(display_2_a), .b(display_2_b), .c(display_2_c),
    .d(display_2_d), .e(display_2_e), .f(display_2_f), .g(display_2_g));
  _7_Segment_Display u_7_segment_display_2 (
    .g(display_2_g), .f(display_2_e), .a(display_2_f), .b(display_2_a), .e(display_2_d), .d(display_2_c),
    .c(display_2_b));  // open: dp
  ROM #(.addrWidth(6), .dataWidth(6)) rom_1 (.addr({in_1, in_2}), .data(out_4));  // open: sel
  ROM #(.addrWidth(6), .dataWidth(6)) rom_2 (.addr({in_1, in_2}), .data(out_6));  // open: sel
  ROM #(.addrWidth(6), .dataWidth(6)) rom_3 (.addr({in_1, in_2}), .data(out_5));  // open: sel

  assign out_3 = {in_1, in_2};

  // Notes on the sheet:
  //   NCR Calculator
  //   24bce123 && 24bce122
  //   contents of rom_1 (hex, n*v repeats v):
  //   1 7*0 1 1 6*0 1 2 1 5*0 1 3 3 1 4*0 1 4 6 4 1 0 0 0 1 5 a a 5 1 0 0 1 6 f 14 f 6 1 0 1 7 15 23 23 15
  //   7 1
  //   contents of rom_2 (hex, n*v repeats v):
  //   1 7*0 1 1 6*0 1 2 1 5*0 1 3 3 1 4*0 1 4 6 4 1 0 0 0 1 5 0 0 5 1 0 0 1 6 5 0 5 6 1 0 1 7 1 5 1 15 7 1
  //   contents of rom_3 (hex, n*v repeats v):
  //   42*0 1 1 6*0 1 2 1 5*0 2 3 3 2
endmodule

module display (
  input  x,
  input  y,
  input  z,
  output a,
  output b,
  output c,
  output d,
  output e,
  output f,
  output g
);

  wire and_1_out, and_2_out, and_3_out, and_4_out, and_5_out, and_6_out, and_7_out, and_8_out, and_9_out,
       and_10_out, and_11_out, and_12_out, and_13_out, and_14_out, and_15_out, and_16_out, not_1_out,
       not_2_out, not_3_out, not_4_out, not_5_out, not_6_out, not_7_out, not_8_out, not_9_out, not_10_out,
       not_11_out, not_12_out, not_13_out, not_14_out, not_15_out, not_16_out, not_17_out, not_18_out,
       not_19_out, not_20_out, not_21_out;

  not not_1 (not_1_out, y);
  not not_2 (not_2_out, z);
  not not_3 (not_3_out, y);
  not not_4 (not_4_out, x);
  not not_5 (not_5_out, z);
  not not_6 (not_6_out, x);
  not not_7 (not_7_out, z);
  not not_8 (not_8_out, y);
  not not_9 (not_9_out, x);
  not not_10 (not_10_out, z);
  not not_11 (not_11_out, z);
  not not_12 (not_12_out, y);
  not not_13 (not_13_out, z);
  not not_14 (not_14_out, y);
  not not_15 (not_15_out, z);
  not not_16 (not_16_out, x);
  not not_17 (not_17_out, z);
  not not_18 (not_18_out, x);
  not not_19 (not_19_out, y);
  not not_20 (not_20_out, z);
  not not_21 (not_21_out, x);
  and and_1 (and_1_out, not_1_out, not_2_out);
  and and_2 (and_2_out, y, z);
  or or_1 (b, not_3_out, z, x);
  and and_3 (and_3_out, not_4_out, not_5_out);
  and and_4 (and_4_out, not_6_out, y);
  and and_5 (and_5_out, y, not_7_out);
  and and_6 (and_6_out, x, not_8_out, z);
  and and_7 (and_7_out, not_9_out, not_10_out);
  and and_8 (and_8_out, y, not_11_out);
  and and_9 (and_9_out, not_12_out, not_13_out);
  and and_10 (and_10_out, x, not_14_out);
  and and_11 (and_11_out, x, not_15_out);
  and and_12 (and_12_out, not_16_out, not_17_out);
  and and_13 (and_13_out, x, z);
  and and_14 (and_14_out, not_18_out, y);
  and and_15 (and_15_out, x, not_19_out);
  and and_16 (and_16_out, x, not_20_out);
  or or_2 (a, not_21_out, and_1_out, and_2_out);
  or or_3 (c, and_3_out, and_4_out, and_5_out, and_6_out);
  or or_4 (d, and_7_out, and_8_out);
  or or_5 (e, and_9_out, and_10_out, and_11_out);
  or or_6 (f, and_12_out, y, and_13_out);
  or or_7 (g, and_14_out, and_15_out, and_16_out);

  // Notes on the sheet:
  //   Display circuit
endmodule
